# Fritzing sketch CircuitDiagram (saved by Fritzing 0.9.3b)
breadboards: 1

parts:
  Gizwits_WiFi_Witty_ESP-12F1 = Gizwits WiFi Witty ESP-12F [part_number=ESP12E]
  Part1 = Soil Moisture Sensor
  Part2 = Soil Moisture Sensor
  R1 = Resistor [tolerance=±5% resistance=10k package="0805 [SMD]"]
  D1 = Rectifier Diode [part_number=1N4001 package="300 mil [THT]"]
  VCC1 = Battery
  R2 = Resistor [tolerance=±5% resistance=10k package="0805 [SMD]"]
  R3 = Resistor [tolerance=±5% resistance=10k package="0805 [SMD]"]
  C1 = Electrolytic Capacitor [capacitance=100nF voltage=10V package="0807 [SMD, electrolytic]"]
  D2 = Rectifier Diode [part_number=1N4001 package="300 mil [THT]"]
  R4 = Resistor [tolerance=±5% resistance=1k package="0805 [SMD]"]
  R5 = Resistor [tolerance=±5% resistance=1k package="0805 [SMD]"]
  R6 = Resistor [tolerance=±5% resistance=4.7k package="0805 [SMD]"]
  R7 = Resistor [tolerance=±5% resistance=4.7k package="0805 [SMD]"]
  M1 = DC Motor
  M2 = DC Motor
  T1 = LM35 Temperature Sensor [part_number="DHT 11" package="TO92 [THT]"]
  R8 = Resistor [tolerance=±5% resistance=10k package="0805 [SMD]"]
  S1 = SWITCH-MOMENTARY-2 [part_number="Water Level Sensor" package=tactile-switch-1101ne]
  R9 = Resistor [tolerance=±5% resistance=10k package="0805 [SMD]"]
  Q1 = npn-Powertransistor [package="TO220 [THT]"]
  Q2 = npn-Powertransistor [package="TO220 [THT]"]
  R10 = Resistor [tolerance=±5% resistance=1k package="0805 [SMD]"]
  R11 = Resistor [tolerance=±5% resistance=1k package="0805 [SMD]"]
  D4 = Rectifier Diode [part_number=1N4001 package="300 mil [THT]"]
  D6 = Rectifier Diode [part_number=1N4001 package="300 mil [THT]"]

nets:
  N1: Gizwits_WiFi_Witty_ESP-12F1.ADC, D1.cathode, D2.cathode
  N2: Gizwits_WiFi_Witty_ESP-12F1.CH_PD, R1.Pin_1
  N3: Gizwits_WiFi_Witty_ESP-12F1.GPIO16, S1.1
  N4: Gizwits_WiFi_Witty_ESP-12F1.GPIO14, T1.Vout, R8.Pin_0
  N5: Gizwits_WiFi_Witty_ESP-12F1.GPIO12, R10.Pin_1
  N6: Gizwits_WiFi_Witty_ESP-12F1.GPIO13, R11.Pin_1
  N7: Gizwits_WiFi_Witty_ESP-12F1.VCC, R1.Pin_0, VCC1.+, R2.Pin_0, C1.+, M1.pin_1, M2.pin_1, T1.+Vs, S1.2, D4.cathode, D6.cathode
  GND: Gizwits_WiFi_Witty_ESP-12F1.GND, Part1.GND, Part2.GND, VCC1.-, R3.Pin_0, C1.-, R6.Pin_1, R7.Pin_1, T1.GND, R8.Pin_1, R9.Pin_0, Q1.emitter, Q2.emitter
  N8: Gizwits_WiFi_Witty_ESP-12F1.GPIO15, R3.Pin_1
  N9: Gizwits_WiFi_Witty_ESP-12F1.GPIO0, R2.Pin_1
  N10: Gizwits_WiFi_Witty_ESP-12F1.GPIO4, Part1.VCC
  N11: Gizwits_WiFi_Witty_ESP-12F1.GPIO5, Part2.VCC
  N12: Part1.SIG, D1.anode, R4.Pin_0
  N13: Part2.SIG, D2.anode, R5.Pin_1
  N14: R4.Pin_1, R6.Pin_0
  N15: R5.Pin_0, R7.Pin_0
  N16: M1.pin_2, Q1.collector, D6.anode
  N17: M2.pin_2, Q2.collector, D4.anode
  N18: Q1.base, R10.Pin_0
  N19: Q2.base, R11.Pin_0
