# Fritzing sketch Circuit_HC-SR04 (saved by Fritzing 0.9.3b)
breadboards: 1

parts:
  R10 = Resistor [tolerance=±5% resistance=1k package=THT]
  R2 = Resistor [tolerance=±5% resistance=4.7k package=THT]
  R9 = Resistor [tolerance=±5% resistance=10k package=THT]
  S1 = SWITCH-MOMENTARY-2 [package=tactile-switch-1101ne]
  R5 = Resistor [tolerance=±5% resistance=1k package=THT]
  Q2 = npn-Powertransistor [package="TO220 [THT]"]
  R4 = Resistor [tolerance=±5% resistance=1k package=THT]
  R7 = Resistor [tolerance=±5% resistance=4.7k package=THT]
  D2 = Rectifier Diode [part_number=1N4001 package="300 mil [THT]"]
  R8 = Resistor [tolerance=±5% resistance=10k package=THT]
  R1 = Resistor [tolerance=±5% resistance=4.7k package=THT]
  Part1 = Soil Moisture Sensor
  C1 = Electrolytic Capacitor [capacitance=100nF voltage=10V package="0807 [SMD, electrolytic]"]
  D6 = Rectifier Diode [part_number=1N4001 package="300 mil [THT]"]
  Part2 = Soil Moisture Sensor
  M2 = DC Motor
  D4 = Rectifier Diode [part_number=1N4001 package="300 mil [THT]"]
  Q1 = npn-Powertransistor [package="TO220 [THT]"]
  R3 = Resistor [tolerance=±5% resistance=4.7k package=THT]
  T1 = LM35 Temperature Sensor [part_number="DHT 11" package="TO92 [THT]"]
  M1 = DC Motor
  D1 = Rectifier Diode [part_number=1N4001 package="300 mil [THT]"]
  Gizwits_WiFi_Witty_ESP-12F1 = Gizwits WiFi Witty ESP-12F [part_number=ESP12E]
  R6 = Resistor [tolerance=±5% resistance=4.7k package=THT]
  R11 = Resistor [tolerance=±5% resistance=1k package=THT]
  VCC1 = Battery
  hc-sr1 = hc-sr04  # not connected

nets:
  N1: R10.Pin_0, Q1.base
  N2: R10.Pin_1, Gizwits_WiFi_Witty_ESP-12F1.GPIO12
  N3: R2.Pin_0, S1.2, R1.Pin_0, C1.+, D6.cathode, M2.pin_1, D4.cathode, T1.+Vs, M1.pin_1, Gizwits_WiFi_Witty_ESP-12F1.VCC, VCC1.+
  N4: R2.Pin_1, Gizwits_WiFi_Witty_ESP-12F1.GPIO0
  GND: R9.Pin_0, Q2.emitter, R7.Pin_1, R8.Pin_1, Part1.GND, C1.-, Part2.GND, Q1.emitter, R3.Pin_0, T1.GND, Gizwits_WiFi_Witty_ESP-12F1.GND, R6.Pin_1, VCC1.-
  N5: S1.1, Gizwits_WiFi_Witty_ESP-12F1.GPIO16
  N6: R5.Pin_0, R7.Pin_0
  N7: R5.Pin_1, D2.anode, Part2.SIG
  N8: Q2.base, R11.Pin_0
  N9: Q2.collector, M2.pin_2, D4.anode
  N10: R4.Pin_0, Part1.SIG, D1.anode
  N11: R4.Pin_1, R6.Pin_0
  N12: D2.cathode, D1.cathode, Gizwits_WiFi_Witty_ESP-12F1.ADC
  N13: R8.Pin_0, T1.Vout, Gizwits_WiFi_Witty_ESP-12F1.GPIO14
  N14: R1.Pin_1, Gizwits_WiFi_Witty_ESP-12F1.CH_PD
  N15: Part1.VCC, Gizwits_WiFi_Witty_ESP-12F1.GPIO4
  N16: D6.anode, Q1.collector, M1.pin_2
  N17: Part2.VCC, Gizwits_WiFi_Witty_ESP-12F1.GPIO5
  N18: R3.Pin_1, Gizwits_WiFi_Witty_ESP-12F1.GPIO15
  N19: Gizwits_WiFi_Witty_ESP-12F1.GPIO13, R11.Pin_1
