# Fritzing sketch ProgrammingCircuit (saved by Fritzing 0.9.3b)
breadboards: 1

parts:
  Gizwits_WiFi_Witty_ESP-12F1 = Gizwits WiFi Witty ESP-12F
  R1 = Resistor [tolerance=±5% resistance=10k package="0805 [SMD]"]
  R2 = Resistor [tolerance=±5% resistance=220 part_number="RTS on CP2102" package="0805 [SMD]"]
  R3 = Resistor [tolerance=±5% resistance=10k package="0805 [SMD]"]
  R4 = Resistor [tolerance=±5% resistance=220 part_number="TXD on CP2102" package="0805 [SMD]"]
  R5 = Resistor [tolerance=±5% resistance=220 part_number="RXD on CP2102" package="0805 [SMD]"]
  R6 = Resistor [tolerance=±5% resistance=10k package="0805 [SMD]"]
  R7 = Resistor [tolerance=±5% resistance=220 part_number="DTR on CP2102" package="0805 [SMD]"]
  R8 = Resistor [tolerance=±5% resistance=10k package="0805 [SMD]"]
  VCC1 = Battery
  C1 = Electrolytic Capacitor [capacitance=100nF package="0807 [SMD, electrolytic]"]

nets:
  N1: Gizwits_WiFi_Witty_ESP-12F1.REST, R1.Pin_1, R2.Pin_1
  N2: Gizwits_WiFi_Witty_ESP-12F1.CH_PD, R3.Pin_1
  N3: Gizwits_WiFi_Witty_ESP-12F1.VCC, R1.Pin_0, R3.Pin_0, R6.Pin_0, VCC1.+, C1.+
  N4: Gizwits_WiFi_Witty_ESP-12F1.GND, R8.Pin_0, VCC1.-, C1.-
  N5: Gizwits_WiFi_Witty_ESP-12F1.GPIO15, R8.Pin_1
  N6: Gizwits_WiFi_Witty_ESP-12F1.GPIO0, R6.Pin_1, R7.Pin_1
  N7: Gizwits_WiFi_Witty_ESP-12F1.RXD, R4.Pin_1
  N8: Gizwits_WiFi_Witty_ESP-12F1.TXD, R5.Pin_1
